// Logisim project imm-gen.circ as structural Verilog: 1 circuit, main circuit imm_gen
module imm_gen (
  input  [31:0] inst,
  input  [2:0] ImmSel,
  output [31:0] imm
);

  wire [31:0] imm_se;

  assign imm_se = {{20{inst[31]}}, inst[31:20]};  // Bit_Extender bit_extender_1
  Multiplexer #(.enable("false"), .select(3), .width(32)) multiplexer_1 (
    .in0(imm_se), .in2(inst), .out(imm), .sel(ImmSel));  // open: in1, in3, in4, in5, in6, in7

  // Other names for the same wires on the sheet: imm_1[11:0] = inst[31:20]

  // Notes on the sheet:
  //   INPUTS to your circuit
  //   DON'T CHANGE THE LOCATIONS OF THE INPUTS AND OUTPUTS!
  //   OUTPUT from your circuit
endmodule
